# Fritzing sketch Schematics BLOOMBOX (saved by Fritzing 1.0.1rc)
breadboards: 1

parts:
  U1 = ESP32S-HiLetgo [part_number=ESP32S-HiLetgo]
  DHT1 = DHT11 Humitidy and Temperature Sensor (3 pins)
  U2 = Module 4 Relais 5V [package="Module 4 Relais 5V"]
  IC1 = DS3231MZ Real Time Clock
  SD_card_module1 = SD Card Module
  U3 = MLX90614 [package=to-39]
  F1 = Fan - Ventilador [package=THT]
  F2 = Fan - Ventilador [package=THT]
  VCC1 = 4 x AAA Battery Mount
  Water_Level_Sensor1 = Water Level Sensor
  Componente1 = FC-28 Soil Hygrometer Module - Probe
  부품3 = FC-28 Soil Hygrometer Module
  R1 = Resistor [tolerance=±5% resistance=150 package="0805 [SMD]"]
  LED1 = LED - 5mm [color="Red (633nm)" current=0.030A package="5 mm [THT]"]
  WATER_PUMP1 = water pump/motor  # not connected

nets:
  N1: U1.GPIO32, Water_Level_Sensor1.VCC
  GND: U1.GND, U1.GPIO23, DHT1.Gnd, U2.GND, U2.K1-NF, U2.K2-NF, U2.K3-NF, U2.K4-NF, IC1.Pin_5, SD_card_module1.GND, U3.VSS, VCC1.-, Water_Level_Sensor1.GND, 부품3.GND
  VCC: U1.GPIO13, DHT1.Plus, U2.VCC, IC1.Pin_2, SD_card_module1.+5, U3.VDD, F1.5V, F2.5V, VCC1.+, 부품3.VCC, R1.Pin_1
  N2: U1.GPIO11, IC1.Pin_7, U3.PWM_SDA
  N3: U2.K2-NO, LED1.cathode
  N4: U2.K3-NO, F1.GND
  N5: U2.K4-NO, F2.GND
  N6: IC1.Pin_8, U3.SCL_VZ
  N7: Componente1.POS, 부품3.POS
  N8: Componente1.NEG, 부품3.NEG
  N9: R1.Pin_0, LED1.anode

custom parts:
  ESP32S-HiLetgo: HiLetgo ESP-WROOM-32 ESP32 ESP-32S Development Board 2.4GHz Dual-Mode WiFi + Bluetooth Dual Cores Microcontroller The ESP32 integrated with Antenna switches, RF Balun, power amplifiers, low-noise amplifiers, filters, and management modules, and the entire solution occupies the least area of PCB. 2.4 GHz Wi-Fi plus Bluetooth dual-mode chip, with TSMC Ultra-low power consumption 40nm technology,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
  DHT11 Humitidy and Temperature Sensor (3 pins): DHT11 Humidity and Temperature Sensor (3 pins).
  Module 4 Relais 5V: Module 4 Relais 5V 4x SPD-06VDC-SD-C
  DS3231MZ Real Time Clock: DS3231MZ Real Time Clock. SO-8 surface mount version.
  SD Card Module: SD Card Module Slot Socket Reader For Arduino ARM MCU
  Fan - Ventilador: Ventilador de 2 pines, se encuentra comunmente en computadoras de escritorio
  Water Level Sensor: A water level sensor. This sensor operates at 3V to 5V. The Sig (signal) pin outputs an analogue signal that is in proportion to the amount of water in contact with the sensor.
  FC-28 Soil Hygrometer Module - Probe: The FC-28 is a soil hygrometer module that uses the Texas Instruments LM393 comparator chip to provide an analog measurement of soil humidity.
  FC-28 Soil Hygrometer Module: The FC-28 is a soil hygrometer module that uses the Texas Instruments LM393 comparator chip to provide an analog measurement of soil humidity. The digital output is high when soil moisture is over a certain threshold, as determined by adjusting the potentiometer.
  water pump/motor: WATER PUMP BY ARDUBLOCKTR

// code stored in the sketch: BLOOMBOX.ino
#include <Wire.h>
#include <DHT.h>
#include "RTClib.h"
#include <Adafruit_MLX90614.h>


#define DHTPIN 0         // DHT11 connected to GPIO0
#define DHTTYPE DHT11    // DHT 11
//#define RELAY_PIN1 4     // Relay connected 
//#define RELAY_PIN2 16    // Relay connected
#define RELAY_PIN3 17    // Relay connected
#define RELAY_PIN4 5     // Relay connected
#define TEMP_LOW_THRESHOLD 14.0 // Temperature threshold
#define TEMP_HIGH_THRESHOLD 14.5 // Temperature threshold
#define WATER_LEVEL_PIN 35  // Water level sensor connected to GPIO35
#define WATER_SENSOR_POWER_PIN 32  // Power pin for the water level sensor connected to GPIO32
#define SOIL_MOISTURE_PIN 34 // Soil moisture sensor connected to GPIO34


#define WATER_LEVEL_MAX 305  // Maximum water level reading
#define WATER_LEVEL_MIN 120     // Minimum water level reading


// Initialize water level percentage variable
int waterLevelPercent;


int waterLevelFinal;
unsigned long waterLevelCheckTime = 60000; // 1 minute, for example
unsigned long lastCheck = 0;


DHT dht(DHTPIN, DHTTYPE);
RTC_DS3231 rtc;
Adafruit_MLX90614 mlx = Adafruit_MLX90614();


void setup() {
  Serial.begin(115200);
  
  dht.begin();


  if (!rtc.begin()) {
    Serial.println("Couldn't find RTC");
    while (1);
  }


  if (!mlx.begin()) {
    Serial.println("Failed to start MLX90614");
    while (1);
  }


  //pinMode(RELAY_PIN1, OUTPUT); // Set the relay pin as output
  //pinMode(RELAY_PIN2, OUTPUT); // Set the relay pin as output
  pinMode(RELAY_PIN3, OUTPUT); // Set the relay pin as output
  pinMode(RELAY_PIN4, OUTPUT); // Set the relay pin as output
  pinMode(WATER_LEVEL_PIN, INPUT); // Set the water level pin as input
  pinMode(SOIL_MOISTURE_PIN, INPUT); // Set the soil moisture sensor pin as input
  pinMode(WATER_SENSOR_POWER_PIN, OUTPUT);
  digitalWrite(WATER_SENSOR_POWER_PIN, LOW);  // Initially turn off the sensor
  //digitalWrite(WATER_SENSOR_POWER_PIN, HIGH);



  // Turn off relays initially
  //digitalWrite(RELAY_PIN1, HIGH);
  //digitalWrite(RELAY_PIN2, HIGH);
  digitalWrite(RELAY_PIN3, HIGH);
  digitalWrite(RELAY_PIN4, HIGH);


  if (rtc.lostPower()) {
    Serial.println("RTC lost power, let's set the time!");
    rtc.adjust(DateTime(F(__DATE__), F(__TIME__)));
  }
}


void loop() {
  delay(1000); // Wait a few seconds between measurements


  float humidity = dht.readHumidity(); // Reading humidity
  float ambientTemp = mlx.readAmbientTempC(); // Reading ambient temperature
  int waterLevel = analogRead(WATER_LEVEL_PIN); // Reading water level
  int soilMoisture = analogRead(SOIL_MOISTURE_PIN); // Reading soil moisture


  // Reading water level
  int waterLevelRaw = analogRead(WATER_LEVEL_PIN); 


  // Calibration data
  const int level25 = 205; 
  const int level50 = 255; 
  const int level75 = 280; 


// Check if it's time to calculate the final water level
  if (millis() - lastCheck >= waterLevelCheckTime) {


    digitalWrite(WATER_SENSOR_POWER_PIN, HIGH);  // Turn on the sensor
    delay(30);  // Short delay for power stabilization


    int sum = 0;
    for (int i = 0; i < 5; i++) {
      sum += analogRead(WATER_LEVEL_PIN); // Read water level
      delay(3000); // Wait for 3 seconds
    }


    digitalWrite(WATER_SENSOR_POWER_PIN, LOW);  // Turn off the sensor


    waterLevelFinal = sum / 5; // Calculate average


    if (waterLevelFinal < level25) {
      waterLevelFinal = map(waterLevelFinal, WATER_LEVEL_MIN, level25, 0, 25);
    } else if (waterLevelRaw < level50) {
      waterLevelFinal = map(waterLevelFinal, level25, level50, 25, 50);
    } else if (waterLevelRaw < level75) {
      waterLevelFinal = map(waterLevelFinal, level50, level75, 50, 75);
    } else {
      waterLevelFinal = map(waterLevelFinal, level75, WATER_LEVEL_MAX, 75, 100);
    }


    waterLevelFinal = constrain(waterLevelFinal, 0, 100); // Constrain to 0-100%



    // Print the final water level
    Serial.print("Final Water Level: ");
    Serial.println(waterLevelFinal);


    lastCheck = millis(); // Update the last check time
  }


// Convert raw readings to percentage based on calibration data
  if (waterLevelRaw < level25) {
    waterLevelPercent = map(waterLevelRaw, WATER_LEVEL_MIN, level25, 0, 25);
  } else if (waterLevelRaw < level50) {
    waterLevelPercent = map(waterLevelRaw, level25, level50, 25, 50);
  } else if (waterLevelRaw < level75) {
    waterLevelPercent = map(waterLevelRaw, level50, level75, 50, 75);
  } else {
    waterLevelPercent = map(waterLevelRaw, level75, WATER_LEVEL_MAX, 75, 100);
  }


  waterLevelPercent = constrain(waterLevelPercent, 0, 100); // Constrain to 0-100%



  if (isnan(humidity)) {
    Serial.println("Failed to read from DHT sensor!");
    return;
  }


  DateTime now = rtc.now(); // Get current time


  // Print the humidity, ambient temperature and time
  Serial.print(now.year(), DEC);
  Serial.print('/');
  Serial.print(now.month(), DEC);
  Serial.print('/');
  Serial.print(now.day(), DEC);
  Serial.print(" ");
  Serial.print(now.hour(), DEC);
  Serial.print(':');
  Serial.print(now.minute(), DEC);
  Serial.print(':');
  Serial.print(now.second(), DEC);
  Serial.print(" - Humidity: ");
  Serial.print(humidity);
  Serial.print(" %, Ambient Temp: ");
  Serial.print(ambientTemp);
  Serial.print(" C");
  Serial.print(", Water Level: ");
  Serial.print(waterLevel);
  Serial.print(", Water Level Percent: ");
  Serial.print(waterLevelPercent);
  Serial.print(" %");
  Serial.print(", Soil Moisture: ");
  Serial.println(soilMoisture);


  // Control the relays based on temperature
  if (ambientTemp > TEMP_HIGH_THRESHOLD) {
    digitalWrite(RELAY_PIN3, LOW); // Turn on relay
    digitalWrite(RELAY_PIN4, LOW); // Turn on relay 
  } else if (ambientTemp <= TEMP_LOW_THRESHOLD) {
    digitalWrite(RELAY_PIN3, HIGH); // Turn off relay 
    digitalWrite(RELAY_PIN4, HIGH); // Turn off relay 
  }
}
